// Logisim project 加法器.circ as structural Verilog
module \半加器  (
  input  in_1,
  input  in_2,
  output out_3,
  output out_4
);

  wire and_1_out, and_2_out, not_1_out, not_2_out;

  not not_1 (not_1_out, in_1);
  not not_2 (not_2_out, in_2);
  and and_1 (and_1_out, not_1_out, in_2);
  and and_2 (and_2_out, in_1, not_2_out);
  and and_3 (out_4, in_2, in_1);
  or or_1 (out_3, and_1_out, and_2_out);
endmodule

module \全加  (
  input  in_1,
  input  in_2,
  input  in_3,
  output out_4,
  output out_5
);

  wire \半加器_1_out_3 , \半加器_1_out_4 , \半加器_2_out_4 ;

  \半加器  \u_半加器_1  (.in_1(in_2), .in_2(in_3), .out_3(\半加器_1_out_3 ), .out_4(\半加器_1_out_4 ));
  \半加器  \u_半加器_2  (.in_1(in_1), .in_2(\半加器_1_out_3 ), .out_3(out_4), .out_4(\半加器_2_out_4 ));
  or or_1 (out_5, \半加器_2_out_4 , \半加器_1_out_4 );
endmodule

module \_8加法  (
  input  in_1,
  input  in_2,
  input  in_3,
  input  in_4,
  input  in_5,
  input  in_6,
  input  in_7,
  input  in_8,
  input  in_9,
  input  in_10,
  input  in_11,
  input  in_12,
  input  in_13,
  input  in_14,
  input  in_15,
  input  in_16,
  output out_17,
  output out_18,
  output out_19,
  output out_20,
  output out_21,
  output out_22,
  output out_23,
  output out_24,
  output out_25
);

  wire \全加_1_out_5 , \全加_2_out_5 , \全加_3_out_5 , \全加_4_out_5 , \全加_5_out_5 , \全加_6_out_5 , \全加_7_out_5 ;

  \全加  \u_全加_1  (.in_1(in_7), .in_2(\全加_2_out_5 ), .in_3(in_15), .out_4(out_24), .out_5(\全加_1_out_5 ));
  \全加  \u_全加_2  (.in_1(1'b0), .in_2(in_8), .in_3(in_16), .out_4(out_25), .out_5(\全加_2_out_5 ));
  \全加  \u_全加_3  (.in_1(\全加_4_out_5 ), .in_2(in_5), .in_3(in_13), .out_4(out_22), .out_5(\全加_3_out_5 ));
  \全加  \u_全加_4  (.in_1(\全加_1_out_5 ), .in_2(in_6), .in_3(in_14), .out_4(out_23), .out_5(\全加_4_out_5 ));
  \全加  \u_全加_5  (.in_1(\全加_3_out_5 ), .in_2(in_4), .in_3(in_12), .out_4(out_21), .out_5(\全加_5_out_5 ));
  \全加  \u_全加_6  (.in_1(\全加_7_out_5 ), .in_2(in_2), .in_3(in_10), .out_4(out_19), .out_5(\全加_6_out_5 ));
  \全加  \u_全加_7  (.in_1(\全加_5_out_5 ), .in_2(in_3), .in_3(in_11), .out_4(out_20), .out_5(\全加_7_out_5 ));
  \全加  \u_全加_8  (.in_1(\全加_6_out_5 ), .in_2(in_1), .in_3(in_9), .out_4(out_18), .out_5(out_17));
endmodule

module alu (
  output out_1
);

  wire c8_1_out_10, c8_1_out_11, c8_1_out_12, c8_1_out_13, c8_1_out_14, c8_1_out_15, c8_1_out_16,
       c8_1_out_17, c8_3_out_10, c8_3_out_11, c8_3_out_12, c8_3_out_13, c8_3_out_14, c8_3_out_15,
       c8_3_out_16, c8_3_out_17, c8_4_out_10, c8_4_out_11, c8_4_out_12, c8_4_out_13, c8_4_out_14,
       c8_4_out_15, c8_4_out_16, c8_4_out_17, c8_5_out_10, c8_5_out_11, c8_5_out_12, c8_5_out_13,
       c8_5_out_14, c8_5_out_15, c8_5_out_16, c8_5_out_17, c8_6_out_10, c8_6_out_11, c8_6_out_12,
       c8_6_out_13, c8_6_out_14, c8_6_out_15, c8_6_out_16, c8_6_out_17, \n8加法_1_out_18 , \n8加法_1_out_19 ,
       \n8加法_1_out_20 , \n8加法_1_out_21 , \n8加法_1_out_22 , \n8加法_1_out_23 , \n8加法_1_out_24 , \n8加法_1_out_25 ;

  C8 c8_1 (
    .in_2(c8_3_out_17), .in_3(c8_3_out_16), .in_4(c8_3_out_15), .in_5(c8_3_out_14), .in_6(c8_3_out_13),
    .in_7(c8_3_out_12), .in_8(c8_3_out_11), .in_9(c8_3_out_10), .out_10(c8_1_out_10), .out_11(c8_1_out_11),
    .out_12(c8_1_out_12), .out_13(c8_1_out_13), .out_14(c8_1_out_14), .out_15(c8_1_out_15),
    .out_16(c8_1_out_16), .out_17(c8_1_out_17));  // open: in_1
  C8 c8_2 (
    .in_2(\n8加法_1_out_25 ), .in_3(\n8加法_1_out_24 ), .in_4(\n8加法_1_out_23 ), .in_5(\n8加法_1_out_22 ),
    .in_6(\n8加法_1_out_21 ), .in_7(\n8加法_1_out_20 ), .in_8(\n8加法_1_out_19 ), .in_9(\n8加法_1_out_18 ),
    .out_10(c8_1_out_17), .out_11(c8_1_out_16), .out_12(c8_1_out_15), .out_13(c8_1_out_14),
    .out_14(c8_1_out_13), .out_15(c8_1_out_12), .out_16(c8_1_out_11), .out_17(c8_1_out_10));  // open: in_1
  C8 c8_3 (
    .in_2(c8_5_out_17), .in_3(c8_5_out_16), .in_4(c8_5_out_15), .in_5(c8_5_out_14), .in_6(c8_5_out_13),
    .in_7(c8_5_out_12), .in_8(c8_5_out_11), .in_9(c8_5_out_10), .out_10(c8_3_out_10), .out_11(c8_3_out_11),
    .out_12(c8_3_out_12), .out_13(c8_3_out_13), .out_14(c8_3_out_14), .out_15(c8_3_out_15),
    .out_16(c8_3_out_16), .out_17(c8_3_out_17));  // open: in_1
  \_8加法  \u_8加法_1  (
    .in_1(c8_4_out_10), .in_2(c8_4_out_11), .in_3(c8_4_out_12), .in_4(c8_4_out_13), .in_5(c8_4_out_14),
    .in_6(c8_4_out_15), .in_7(c8_4_out_16), .in_8(c8_4_out_17), .in_9(c8_6_out_10), .in_10(c8_6_out_11),
    .in_11(c8_6_out_12), .in_12(c8_6_out_13), .in_13(c8_6_out_14), .in_14(c8_6_out_15), .in_15(c8_6_out_16),
    .in_16(c8_6_out_17), .out_17(out_1), .out_18(\n8加法_1_out_18 ), .out_19(\n8加法_1_out_19 ),
    .out_20(\n8加法_1_out_20 ), .out_21(\n8加法_1_out_21 ), .out_22(\n8加法_1_out_22 ), .out_23(\n8加法_1_out_23 ),
    .out_24(\n8加法_1_out_24 ), .out_25(\n8加法_1_out_25 ));
  C8 c8_4 (
    .in_2(c8_5_out_10), .in_3(c8_5_out_11), .in_4(c8_5_out_12), .in_5(c8_5_out_13), .in_6(c8_5_out_14),
    .in_7(c8_5_out_15), .in_8(c8_5_out_16), .in_9(c8_5_out_17), .out_10(c8_4_out_10), .out_11(c8_4_out_11),
    .out_12(c8_4_out_12), .out_13(c8_4_out_13), .out_14(c8_4_out_14), .out_15(c8_4_out_15),
    .out_16(c8_4_out_16), .out_17(c8_4_out_17));  // open: in_1
  C8 c8_5 (
    .in_2(c8_1_out_17), .in_3(c8_1_out_16), .in_4(c8_1_out_15), .in_5(c8_1_out_14), .in_6(c8_1_out_13),
    .in_7(c8_1_out_12), .in_8(c8_1_out_11), .in_9(c8_1_out_10), .out_10(c8_5_out_10), .out_11(c8_5_out_11),
    .out_12(c8_5_out_12), .out_13(c8_5_out_13), .out_14(c8_5_out_14), .out_15(c8_5_out_15),
    .out_16(c8_5_out_16), .out_17(c8_5_out_17));  // open: in_1
  C8 c8_6 (
    .in_2(c8_5_out_10), .in_3(c8_5_out_11), .in_4(c8_5_out_12), .in_5(c8_5_out_13), .in_6(c8_5_out_14),
    .in_7(c8_5_out_15), .in_8(c8_5_out_16), .in_9(c8_5_out_17), .out_10(c8_6_out_10), .out_11(c8_6_out_11),
    .out_12(c8_6_out_12), .out_13(c8_6_out_13), .out_14(c8_6_out_14), .out_15(c8_6_out_15),
    .out_16(c8_6_out_16), .out_17(c8_6_out_17));  // open: in_1
endmodule

module \验证  (
  input  in_1,
  input  in_2,
  input  in_3,
  input  in_4,
  input  in_5,
  input  in_6,
  input  in_7,
  input  in_8,
  input  in_9,
  input  in_10,
  input  in_11,
  input  in_12,
  input  in_13,
  input  in_14,
  input  in_15,
  input  in_16,
  input  in_17,
  input  in_18,
  input  in_19,
  input  in_20,
  input  in_21,
  input  in_22,
  input  in_23,
  input  in_24,
  input  in_25,
  input  in_26,
  input  in_27,
  input  in_28,
  input  in_29,
  input  in_30,
  input  in_31,
  input  in_32,
  input  in_33,
  input  in_34,
  output out_35
);

  wire c8_1_out_10, c8_1_out_11, c8_1_out_12, c8_1_out_13, c8_1_out_14, c8_1_out_15, c8_1_out_16,
       c8_1_out_17, clock_1_out, double_16key_1_out_37, double_16key_1_out_38, double_16key_1_out_39,
       double_16key_1_out_40, double_16key_1_out_41, double_16key_1_out_42, double_16key_1_out_43,
       double_16key_1_out_44, n2seg_1_out_10, n2seg_1_out_11, n2seg_1_out_12, n2seg_1_out_13, n2seg_1_out_14,
       n2seg_1_out_15, n2seg_1_out_16, n2seg_1_out_17, n2seg_1_out_18, n2seg_1_out_19, n2seg_1_out_20,
       n2seg_1_out_21, n2seg_1_out_22, n2seg_1_out_23, \n4_16译码器_1_out_5 , \n4_16译码器_1_out_6 ,
       \n4_16译码器_1_out_7 , \n4_16译码器_1_out_8 , \n4_16译码器_1_out_9 , \n4_16译码器_1_out_10 , \n4_16译码器_1_out_11 ,
       \n4_16译码器_1_out_12 , \n4_16译码器_1_out_13 , \n4_16译码器_1_out_14 , \n4_16译码器_1_out_15 ,
       \n4_16译码器_1_out_16 , \n4_16译码器_1_out_17 , \n4_16译码器_1_out_18 , \n4_16译码器_1_out_19 ,
       \n4_16译码器_1_out_20 , \n8加法_1_out_18 , \n8加法_1_out_19 , \n8加法_1_out_20 , \n8加法_1_out_21 ,
       \n8加法_1_out_22 , \n8加法_1_out_23 , \n8加法_1_out_24 , \n8加法_1_out_25 , or_1_out, or_2_out, reg8_1_out_10,
       reg8_1_out_11, reg8_1_out_12, reg8_1_out_13, reg8_1_out_14, reg8_1_out_15, reg8_1_out_16,
       reg8_1_out_17, reg8_2_out_10, reg8_2_out_11, reg8_2_out_12, reg8_2_out_13, reg8_2_out_14,
       reg8_2_out_15, reg8_2_out_16, reg8_2_out_17, reg8_3_out_10, reg8_3_out_11, reg8_3_out_12,
       reg8_3_out_13, reg8_3_out_14, reg8_3_out_15, reg8_3_out_16, reg8_3_out_17, s_r_ff_1_q, s_r_ff_2_q,
       s_r_ff_3_q, s_r_ff_4_q, s_r_ff_5_q, s_r_ff_6_q, s_r_ff_7_q, s_r_ff_8_q, s_r_ff_9_q;
  wire [3:0] counter_1_q;

  double_16key double_16key_1 (
    .in_1(in_1), .in_2(in_2), .in_3(in_3), .in_4(in_4), .in_5(in_5), .in_6(in_6), .in_7(in_7), .in_8(in_8),
    .in_9(in_9), .in_12(in_10), .in_13(in_11), .in_14(in_12), .in_15(in_13), .in_16(in_14), .in_17(in_15),
    .in_18(in_16), .in_19(in_17), .in_20(in_18), .in_21(in_19), .in_22(in_20), .in_23(in_21), .in_24(in_22),
    .in_25(in_23), .in_26(in_26), .in_27(in_27), .in_28(in_28), .in_29(in_29), .in_32(in_30), .in_33(in_31),
    .in_34(in_32), .in_35(in_33), .in_36(in_34), .in_10(s_r_ff_1_q), .in_11(s_r_ff_2_q), .in_30(in_24),
    .in_31(in_25), .out_37(double_16key_1_out_37), .out_38(double_16key_1_out_38),
    .out_39(double_16key_1_out_39), .out_40(double_16key_1_out_40), .out_41(double_16key_1_out_41),
    .out_42(double_16key_1_out_42), .out_43(double_16key_1_out_43), .out_44(double_16key_1_out_44));
  LED led_1 (.in(double_16key_1_out_37));
  LED led_2 (.in(double_16key_1_out_38));
  LED led_3 (.in(double_16key_1_out_41));
  LED led_4 (.in(double_16key_1_out_42));
  LED led_5 (.in(double_16key_1_out_39));
  LED led_6 (.in(double_16key_1_out_40));
  LED led_7 (.in(double_16key_1_out_43));
  LED led_8 (.in(double_16key_1_out_44));
  C8 c8_1 (
    .in_2(double_16key_1_out_44), .in_3(double_16key_1_out_43), .in_4(double_16key_1_out_42),
    .in_5(double_16key_1_out_41), .in_6(double_16key_1_out_40), .in_7(double_16key_1_out_39),
    .in_8(double_16key_1_out_38), .in_9(double_16key_1_out_37), .out_10(c8_1_out_10), .out_11(c8_1_out_11),
    .out_12(c8_1_out_12), .out_13(c8_1_out_13), .out_14(c8_1_out_14), .out_15(c8_1_out_15),
    .out_16(c8_1_out_16), .out_17(c8_1_out_17), .in_1(s_r_ff_3_q));
  S_R_Flip_Flop s_r_ff_1 (
    .Q(s_r_ff_1_q), .preset(\n4_16译码器_1_out_5 ), .reset(\n4_16译码器_1_out_7 ));  // open: S, clk, R, Qn, en
  S_R_Flip_Flop s_r_ff_2 (
    .Q(s_r_ff_2_q), .preset(\n4_16译码器_1_out_8 ), .reset(\n4_16译码器_1_out_10 ));  // open: S, clk, R, Qn, en
  S_R_Flip_Flop s_r_ff_3 (
    .Q(s_r_ff_3_q), .preset(\n4_16译码器_1_out_5 ), .reset(\n4_16译码器_1_out_11 ));  // open: S, clk, R, Qn, en
  C8 c8_2 (
    .in_2(\n8加法_1_out_25 ), .in_3(\n8加法_1_out_24 ), .in_4(\n8加法_1_out_23 ), .in_5(\n8加法_1_out_22 ),
    .in_6(\n8加法_1_out_21 ), .in_7(\n8加法_1_out_20 ), .in_8(\n8加法_1_out_19 ), .in_9(\n8加法_1_out_18 ),
    .out_10(c8_1_out_17), .out_11(c8_1_out_16), .out_12(c8_1_out_15), .out_13(c8_1_out_14),
    .out_14(c8_1_out_13), .out_15(c8_1_out_12), .out_16(c8_1_out_11), .out_17(c8_1_out_10), .in_1(s_r_ff_5_q));
  C8 c8_3 (
    .in_2(reg8_2_out_17), .in_3(reg8_2_out_16), .in_4(reg8_2_out_15), .in_5(reg8_2_out_14),
    .in_6(reg8_2_out_13), .in_7(reg8_2_out_12), .in_8(reg8_2_out_11), .in_9(reg8_2_out_10),
    .out_10(double_16key_1_out_37), .out_11(double_16key_1_out_38), .out_12(double_16key_1_out_39),
    .out_13(double_16key_1_out_40), .out_14(double_16key_1_out_41), .out_15(double_16key_1_out_42),
    .out_16(double_16key_1_out_43), .out_17(double_16key_1_out_44), .in_1(s_r_ff_4_q));
  S_R_Flip_Flop s_r_ff_4 (
    .Q(s_r_ff_4_q), .preset(\n4_16译码器_1_out_14 ), .reset(\n4_16译码器_1_out_20 ));  // open: S, clk, R, Qn, en
  _2seg u_2seg_1 (
    .in_2(double_16key_1_out_37), .in_3(double_16key_1_out_38), .in_4(double_16key_1_out_39),
    .in_5(double_16key_1_out_40), .in_6(double_16key_1_out_41), .in_7(double_16key_1_out_42),
    .in_8(double_16key_1_out_43), .in_9(double_16key_1_out_44), .out_10(n2seg_1_out_10),
    .out_11(n2seg_1_out_11), .out_12(n2seg_1_out_12), .out_13(n2seg_1_out_13), .out_14(n2seg_1_out_14),
    .out_15(n2seg_1_out_15), .out_16(n2seg_1_out_16), .out_17(n2seg_1_out_17), .out_18(n2seg_1_out_18),
    .out_19(n2seg_1_out_19), .out_20(n2seg_1_out_20), .out_21(n2seg_1_out_21), .out_22(n2seg_1_out_22),
    .out_23(n2seg_1_out_23), .in_1(s_r_ff_9_q));
  \_8加法  \u_8加法_1  (
    .in_1(reg8_1_out_10), .in_2(reg8_1_out_11), .in_3(reg8_1_out_12), .in_4(reg8_1_out_13),
    .in_5(reg8_1_out_14), .in_6(reg8_1_out_15), .in_7(reg8_1_out_16), .in_8(reg8_1_out_17),
    .in_9(reg8_3_out_10), .in_10(reg8_3_out_11), .in_11(reg8_3_out_12), .in_12(reg8_3_out_13),
    .in_13(reg8_3_out_14), .in_14(reg8_3_out_15), .in_15(reg8_3_out_16), .in_16(reg8_3_out_17),
    .out_17(out_35), .out_18(\n8加法_1_out_18 ), .out_19(\n8加法_1_out_19 ), .out_20(\n8加法_1_out_20 ),
    .out_21(\n8加法_1_out_21 ), .out_22(\n8加法_1_out_22 ), .out_23(\n8加法_1_out_23 ), .out_24(\n8加法_1_out_24 ),
    .out_25(\n8加法_1_out_25 ));
  reg8 reg8_1 (
    .in_1(reg8_2_out_10), .in_2(reg8_2_out_11), .in_3(reg8_2_out_12), .in_4(reg8_2_out_13),
    .in_5(reg8_2_out_14), .in_6(reg8_2_out_15), .in_7(reg8_2_out_16), .in_9(reg8_2_out_17),
    .in_8(s_r_ff_7_q), .out_10(reg8_1_out_10), .out_11(reg8_1_out_11), .out_12(reg8_1_out_12),
    .out_13(reg8_1_out_13), .out_14(reg8_1_out_14), .out_15(reg8_1_out_15), .out_16(reg8_1_out_16),
    .out_17(reg8_1_out_17));
  reg8 reg8_2 (
    .in_1(c8_1_out_17), .in_2(c8_1_out_16), .in_3(c8_1_out_15), .in_4(c8_1_out_14), .in_5(c8_1_out_13),
    .in_6(c8_1_out_12), .in_7(c8_1_out_11), .in_9(c8_1_out_10), .in_8(s_r_ff_6_q), .out_10(reg8_2_out_10),
    .out_11(reg8_2_out_11), .out_12(reg8_2_out_12), .out_13(reg8_2_out_13), .out_14(reg8_2_out_14),
    .out_15(reg8_2_out_15), .out_16(reg8_2_out_16), .out_17(reg8_2_out_17));
  S_R_Flip_Flop s_r_ff_5 (
    .Q(s_r_ff_5_q), .preset(\n4_16译码器_1_out_12 ), .reset(\n4_16译码器_1_out_14 ));  // open: S, clk, R, Qn, en
  S_R_Flip_Flop s_r_ff_6 (.Q(s_r_ff_6_q), .preset(or_1_out), .reset(or_2_out));  // open: S, clk, R, Qn, en
  or or_1 (or_1_out, \n4_16译码器_1_out_9 , \n4_16译码器_1_out_13 , \n4_16译码器_1_out_6 );
  reg8 reg8_3 (
    .in_1(reg8_2_out_10), .in_2(reg8_2_out_11), .in_3(reg8_2_out_12), .in_4(reg8_2_out_13),
    .in_5(reg8_2_out_14), .in_6(reg8_2_out_15), .in_7(reg8_2_out_16), .in_9(reg8_2_out_17),
    .in_8(s_r_ff_8_q), .out_10(reg8_3_out_10), .out_11(reg8_3_out_11), .out_12(reg8_3_out_12),
    .out_13(reg8_3_out_13), .out_14(reg8_3_out_14), .out_15(reg8_3_out_15), .out_16(reg8_3_out_16),
    .out_17(reg8_3_out_17));
  S_R_Flip_Flop s_r_ff_7 (
    .Q(s_r_ff_7_q), .preset(\n4_16译码器_1_out_7 ), .reset(\n4_16译码器_1_out_8 ));  // open: S, clk, R, Qn, en
  or or_2 (or_2_out, \n4_16译码器_1_out_7 , \n4_16译码器_1_out_14 , \n4_16译码器_1_out_10 );
  _7_Segment_Display #(.active("false")) u_7_segment_display_1 (
    .g(n2seg_1_out_16), .f(n2seg_1_out_15), .a(n2seg_1_out_10), .b(n2seg_1_out_11), .e(n2seg_1_out_14),
    .d(n2seg_1_out_13), .c(n2seg_1_out_12), .dp(1'b1));
  S_R_Flip_Flop s_r_ff_8 (
    .Q(s_r_ff_8_q), .preset(\n4_16译码器_1_out_11 ), .reset(\n4_16译码器_1_out_12 ));  // open: S, clk, R, Qn, en
  _7_Segment_Display #(.active("false")) u_7_segment_display_2 (
    .g(n2seg_1_out_23), .f(n2seg_1_out_22), .a(n2seg_1_out_17), .b(n2seg_1_out_18), .e(n2seg_1_out_21),
    .d(n2seg_1_out_20), .c(n2seg_1_out_19), .dp(1'b1));
  S_R_Flip_Flop s_r_ff_9 (
    .Q(s_r_ff_9_q), .preset(\n4_16译码器_1_out_5 ), .reset(\n4_16译码器_1_out_20 ));  // open: S, clk, R, Qn, en
  Counter #(.width(4), .max('hf)) counter_1 (.Q(counter_1_q), .clk(clock_1_out));  // open: load, D, count, carry, clr
  Clock clock_1 (.out(clock_1_out));
  \_4_16译码器  \u_4_16译码器_1  (
    .in_1(counter_1_q[0]), .in_2(counter_1_q[1]), .in_3(counter_1_q[2]), .in_4(counter_1_q[3]),
    .out_5(\n4_16译码器_1_out_5 ), .out_6(\n4_16译码器_1_out_6 ), .out_7(\n4_16译码器_1_out_7 ),
    .out_8(\n4_16译码器_1_out_8 ), .out_9(\n4_16译码器_1_out_9 ), .out_10(\n4_16译码器_1_out_10 ),
    .out_11(\n4_16译码器_1_out_11 ), .out_12(\n4_16译码器_1_out_12 ), .out_13(\n4_16译码器_1_out_13 ),
    .out_14(\n4_16译码器_1_out_14 ), .out_15(\n4_16译码器_1_out_15 ), .out_16(\n4_16译码器_1_out_16 ),
    .out_17(\n4_16译码器_1_out_17 ), .out_18(\n4_16译码器_1_out_18 ), .out_19(\n4_16译码器_1_out_19 ),
    .out_20(\n4_16译码器_1_out_20 ));
endmodule

module \验证2  (
  input  in_1,
  input  in_2,
  input  in_3,
  input  in_4,
  input  in_5,
  input  in_6,
  input  in_7,
  input  in_8,
  input  in_9,
  input  in_10,
  input  in_11,
  input  in_12,
  input  in_13,
  input  in_14,
  input  in_15,
  input  in_16,
  input  in_17,
  input  in_18,
  input  in_19,
  input  in_20,
  input  in_21,
  input  in_22,
  input  in_23,
  input  in_24,
  input  in_25,
  input  in_26,
  input  in_27,
  input  in_28,
  input  in_29,
  input  in_30,
  input  in_31,
  input  in_32,
  input  in_33,
  input  in_34,
  output out_35
);

  wire c8_1_out_10, c8_1_out_11, c8_1_out_12, c8_1_out_13, c8_1_out_14, c8_1_out_15, c8_1_out_16,
       c8_1_out_17, clock_1_out, double_16key_1_out_37, double_16key_1_out_38, double_16key_1_out_39,
       double_16key_1_out_40, double_16key_1_out_41, double_16key_1_out_42, double_16key_1_out_43,
       double_16key_1_out_44, n2seg_1_out_10, n2seg_1_out_11, n2seg_1_out_12, n2seg_1_out_13, n2seg_1_out_14,
       n2seg_1_out_15, n2seg_1_out_16, n2seg_1_out_17, n2seg_1_out_18, n2seg_1_out_19, n2seg_1_out_20,
       n2seg_1_out_21, n2seg_1_out_22, n2seg_1_out_23, \n8加法_1_out_18 , \n8加法_1_out_19 , \n8加法_1_out_20 ,
       \n8加法_1_out_21 , \n8加法_1_out_22 , \n8加法_1_out_23 , \n8加法_1_out_24 , \n8加法_1_out_25 , reg8_1_out_10,
       reg8_1_out_11, reg8_1_out_12, reg8_1_out_13, reg8_1_out_14, reg8_1_out_15, reg8_1_out_16,
       reg8_1_out_17, reg8_2_out_10, reg8_2_out_11, reg8_2_out_12, reg8_2_out_13, reg8_2_out_14,
       reg8_2_out_15, reg8_2_out_16, reg8_2_out_17, reg8_3_out_10, reg8_3_out_11, reg8_3_out_12,
       reg8_3_out_13, reg8_3_out_14, reg8_3_out_15, reg8_3_out_16, reg8_3_out_17;
  wire [3:0] counter_1_q;
  wire [8:0] rom_1_data;

  double_16key double_16key_1 (
    .in_1(in_1), .in_2(in_2), .in_3(in_3), .in_4(in_4), .in_5(in_5), .in_6(in_6), .in_7(in_7), .in_8(in_8),
    .in_9(in_9), .in_12(in_10), .in_13(in_11), .in_14(in_12), .in_15(in_13), .in_16(in_14), .in_17(in_15),
    .in_18(in_16), .in_19(in_17), .in_20(in_18), .in_21(in_19), .in_22(in_20), .in_23(in_21), .in_24(in_22),
    .in_25(in_23), .in_26(in_26), .in_27(in_27), .in_28(in_28), .in_29(in_29), .in_32(in_30), .in_33(in_31),
    .in_34(in_32), .in_35(in_33), .in_36(in_34), .in_10(rom_1_data[8]), .in_11(rom_1_data[7]), .in_30(in_24),
    .in_31(in_25), .out_37(double_16key_1_out_37), .out_38(double_16key_1_out_38),
    .out_39(double_16key_1_out_39), .out_40(double_16key_1_out_40), .out_41(double_16key_1_out_41),
    .out_42(double_16key_1_out_42), .out_43(double_16key_1_out_43), .out_44(double_16key_1_out_44));
  LED led_1 (.in(double_16key_1_out_37));
  LED led_2 (.in(double_16key_1_out_38));
  LED led_3 (.in(double_16key_1_out_41));
  LED led_4 (.in(double_16key_1_out_42));
  LED led_5 (.in(double_16key_1_out_39));
  LED led_6 (.in(double_16key_1_out_40));
  LED led_7 (.in(double_16key_1_out_43));
  LED led_8 (.in(double_16key_1_out_44));
  C8 c8_1 (
    .in_2(double_16key_1_out_44), .in_3(double_16key_1_out_43), .in_4(double_16key_1_out_42),
    .in_5(double_16key_1_out_41), .in_6(double_16key_1_out_40), .in_7(double_16key_1_out_39),
    .in_8(double_16key_1_out_38), .in_9(double_16key_1_out_37), .out_10(c8_1_out_10), .out_11(c8_1_out_11),
    .out_12(c8_1_out_12), .out_13(c8_1_out_13), .out_14(c8_1_out_14), .out_15(c8_1_out_15),
    .out_16(c8_1_out_16), .out_17(c8_1_out_17), .in_1(rom_1_data[6]));
  C8 c8_2 (
    .in_2(\n8加法_1_out_25 ), .in_3(\n8加法_1_out_24 ), .in_4(\n8加法_1_out_23 ), .in_5(\n8加法_1_out_22 ),
    .in_6(\n8加法_1_out_21 ), .in_7(\n8加法_1_out_20 ), .in_8(\n8加法_1_out_19 ), .in_9(\n8加法_1_out_18 ),
    .out_10(c8_1_out_17), .out_11(c8_1_out_16), .out_12(c8_1_out_15), .out_13(c8_1_out_14),
    .out_14(c8_1_out_13), .out_15(c8_1_out_12), .out_16(c8_1_out_11), .out_17(c8_1_out_10),
    .in_1(rom_1_data[4]));
  C8 c8_3 (
    .in_2(reg8_2_out_17), .in_3(reg8_2_out_16), .in_4(reg8_2_out_15), .in_5(reg8_2_out_14),
    .in_6(reg8_2_out_13), .in_7(reg8_2_out_12), .in_8(reg8_2_out_11), .in_9(reg8_2_out_10),
    .out_10(double_16key_1_out_37), .out_11(double_16key_1_out_38), .out_12(double_16key_1_out_39),
    .out_13(double_16key_1_out_40), .out_14(double_16key_1_out_41), .out_15(double_16key_1_out_42),
    .out_16(double_16key_1_out_43), .out_17(double_16key_1_out_44), .in_1(rom_1_data[5]));
  _2seg u_2seg_1 (
    .in_2(double_16key_1_out_37), .in_3(double_16key_1_out_38), .in_4(double_16key_1_out_39),
    .in_5(double_16key_1_out_40), .in_6(double_16key_1_out_41), .in_7(double_16key_1_out_42),
    .in_8(double_16key_1_out_43), .in_9(double_16key_1_out_44), .out_10(n2seg_1_out_10),
    .out_11(n2seg_1_out_11), .out_12(n2seg_1_out_12), .out_13(n2seg_1_out_13), .out_14(n2seg_1_out_14),
    .out_15(n2seg_1_out_15), .out_16(n2seg_1_out_16), .out_17(n2seg_1_out_17), .out_18(n2seg_1_out_18),
    .out_19(n2seg_1_out_19), .out_20(n2seg_1_out_20), .out_21(n2seg_1_out_21), .out_22(n2seg_1_out_22),
    .out_23(n2seg_1_out_23), .in_1(rom_1_data[0]));
  \_8加法  \u_8加法_1  (
    .in_1(reg8_1_out_10), .in_2(reg8_1_out_11), .in_3(reg8_1_out_12), .in_4(reg8_1_out_13),
    .in_5(reg8_1_out_14), .in_6(reg8_1_out_15), .in_7(reg8_1_out_16), .in_8(reg8_1_out_17),
    .in_9(reg8_3_out_10), .in_10(reg8_3_out_11), .in_11(reg8_3_out_12), .in_12(reg8_3_out_13),
    .in_13(reg8_3_out_14), .in_14(reg8_3_out_15), .in_15(reg8_3_out_16), .in_16(reg8_3_out_17),
    .out_17(out_35), .out_18(\n8加法_1_out_18 ), .out_19(\n8加法_1_out_19 ), .out_20(\n8加法_1_out_20 ),
    .out_21(\n8加法_1_out_21 ), .out_22(\n8加法_1_out_22 ), .out_23(\n8加法_1_out_23 ), .out_24(\n8加法_1_out_24 ),
    .out_25(\n8加法_1_out_25 ));
  reg8 reg8_1 (
    .in_1(reg8_2_out_10), .in_2(reg8_2_out_11), .in_3(reg8_2_out_12), .in_4(reg8_2_out_13),
    .in_5(reg8_2_out_14), .in_6(reg8_2_out_15), .in_7(reg8_2_out_16), .in_9(reg8_2_out_17),
    .in_8(rom_1_data[2]), .out_10(reg8_1_out_10), .out_11(reg8_1_out_11), .out_12(reg8_1_out_12),
    .out_13(reg8_1_out_13), .out_14(reg8_1_out_14), .out_15(reg8_1_out_15), .out_16(reg8_1_out_16),
    .out_17(reg8_1_out_17));
  reg8 reg8_2 (
    .in_1(c8_1_out_17), .in_2(c8_1_out_16), .in_3(c8_1_out_15), .in_4(c8_1_out_14), .in_5(c8_1_out_13),
    .in_6(c8_1_out_12), .in_7(c8_1_out_11), .in_9(c8_1_out_10), .in_8(rom_1_data[3]), .out_10(reg8_2_out_10),
    .out_11(reg8_2_out_11), .out_12(reg8_2_out_12), .out_13(reg8_2_out_13), .out_14(reg8_2_out_14),
    .out_15(reg8_2_out_15), .out_16(reg8_2_out_16), .out_17(reg8_2_out_17));
  reg8 reg8_3 (
    .in_1(reg8_2_out_10), .in_2(reg8_2_out_11), .in_3(reg8_2_out_12), .in_4(reg8_2_out_13),
    .in_5(reg8_2_out_14), .in_6(reg8_2_out_15), .in_7(reg8_2_out_16), .in_9(reg8_2_out_17),
    .in_8(rom_1_data[1]), .out_10(reg8_3_out_10), .out_11(reg8_3_out_11), .out_12(reg8_3_out_12),
    .out_13(reg8_3_out_13), .out_14(reg8_3_out_14), .out_15(reg8_3_out_15), .out_16(reg8_3_out_16),
    .out_17(reg8_3_out_17));
  _7_Segment_Display #(.active("false")) u_7_segment_display_1 (
    .g(n2seg_1_out_16), .f(n2seg_1_out_15), .a(n2seg_1_out_10), .b(n2seg_1_out_11), .e(n2seg_1_out_14),
    .d(n2seg_1_out_13), .c(n2seg_1_out_12), .dp(1'b1));
  _7_Segment_Display #(.active("false")) u_7_segment_display_2 (
    .g(n2seg_1_out_23), .f(n2seg_1_out_22), .a(n2seg_1_out_17), .b(n2seg_1_out_18), .e(n2seg_1_out_21),
    .d(n2seg_1_out_20), .c(n2seg_1_out_19), .dp(1'b1));
  Counter #(.width(4), .max('hf)) counter_1 (.Q(counter_1_q), .clk(clock_1_out));  // open: load, D, count, carry, clr
  Clock clock_1 (.out(clock_1_out));
  ROM #(.addrWidth(4), .dataWidth(9)) rom_1 (.addr(counter_1_q), .data(rom_1_data));  // open: sel

  // Notes on the sheet:
  //   contents of rom_1 (hex, n*v repeats v):
  //   141 149 45 c1 c9 13 19 8*21
endmodule

module \验证3  (
  input  in_1,
  input  in_2,
  input  in_3,
  input  in_4,
  input  in_5,
  input  in_6,
  input  in_7,
  input  in_8,
  input  in_9,
  input  in_10,
  input  in_11,
  input  in_12,
  input  in_13,
  input  in_14,
  input  in_15,
  input  in_16,
  input  in_17,
  input  in_18,
  input  in_19,
  input  in_20,
  input  in_21,
  input  in_22,
  input  in_23,
  input  in_24,
  input  in_25,
  input  in_26,
  input  in_27,
  input  in_28,
  input  in_29,
  input  in_30,
  input  in_31,
  input  in_32,
  input  in_33,
  input  in_34,
  output out_35
);

  wire c8_1_out_10, c8_1_out_11, c8_1_out_12, c8_1_out_13, c8_1_out_14, c8_1_out_15, c8_1_out_16,
       c8_1_out_17, clock_1_out, double_16key_1_out_37, double_16key_1_out_38, double_16key_1_out_39,
       double_16key_1_out_40, double_16key_1_out_41, double_16key_1_out_42, double_16key_1_out_43,
       double_16key_1_out_44, n2seg_1_out_10, n2seg_1_out_11, n2seg_1_out_12, n2seg_1_out_13, n2seg_1_out_14,
       n2seg_1_out_15, n2seg_1_out_16, n2seg_1_out_17, n2seg_1_out_18, n2seg_1_out_19, n2seg_1_out_20,
       n2seg_1_out_21, n2seg_1_out_22, n2seg_1_out_23, \n8加法_1_out_18 , \n8加法_1_out_19 , \n8加法_1_out_20 ,
       \n8加法_1_out_21 , \n8加法_1_out_22 , \n8加法_1_out_23 , \n8加法_1_out_24 , \n8加法_1_out_25 , reg8_1_out_10,
       reg8_1_out_11, reg8_1_out_12, reg8_1_out_13, reg8_1_out_14, reg8_1_out_15, reg8_1_out_16,
       reg8_1_out_17, reg8_2_out_10, reg8_2_out_11, reg8_2_out_12, reg8_2_out_13, reg8_2_out_14,
       reg8_2_out_15, reg8_2_out_16, reg8_2_out_17, reg8_3_out_10, reg8_3_out_11, reg8_3_out_12,
       reg8_3_out_13, reg8_3_out_14, reg8_3_out_15, reg8_3_out_16, reg8_3_out_17;
  wire [4:2] rom_1_data;
  wire [5:0] counter_1_q;
  wire [6:3] rom_1_data_2;
  wire [10:0] rom_2_data;

  double_16key double_16key_1 (
    .in_1(in_1), .in_2(in_2), .in_3(in_3), .in_4(in_4), .in_5(in_5), .in_6(in_6), .in_7(in_7), .in_8(in_8),
    .in_9(in_9), .in_12(in_10), .in_13(in_11), .in_14(in_12), .in_15(in_13), .in_16(in_14), .in_17(in_15),
    .in_18(in_16), .in_19(in_17), .in_20(in_18), .in_21(in_19), .in_22(in_20), .in_23(in_21), .in_24(in_22),
    .in_25(in_23), .in_26(in_26), .in_27(in_27), .in_28(in_28), .in_29(in_29), .in_32(in_30), .in_33(in_31),
    .in_34(in_32), .in_35(in_33), .in_36(in_34), .in_10(rom_2_data[8]), .in_11(rom_2_data[7]), .in_30(in_24),
    .in_31(in_25), .out_37(double_16key_1_out_37), .out_38(double_16key_1_out_38),
    .out_39(double_16key_1_out_39), .out_40(double_16key_1_out_40), .out_41(double_16key_1_out_41),
    .out_42(double_16key_1_out_42), .out_43(double_16key_1_out_43), .out_44(double_16key_1_out_44));
  LED led_1 (.in(double_16key_1_out_37));
  LED led_2 (.in(double_16key_1_out_38));
  LED led_3 (.in(double_16key_1_out_41));
  LED led_4 (.in(double_16key_1_out_42));
  LED led_5 (.in(double_16key_1_out_39));
  LED led_6 (.in(double_16key_1_out_40));
  LED led_7 (.in(double_16key_1_out_43));
  LED led_8 (.in(double_16key_1_out_44));
  C8 c8_1 (
    .in_2(double_16key_1_out_44), .in_3(double_16key_1_out_43), .in_4(double_16key_1_out_42),
    .in_5(double_16key_1_out_41), .in_6(double_16key_1_out_40), .in_7(double_16key_1_out_39),
    .in_8(double_16key_1_out_38), .in_9(double_16key_1_out_37), .out_10(c8_1_out_10), .out_11(c8_1_out_11),
    .out_12(c8_1_out_12), .out_13(c8_1_out_13), .out_14(c8_1_out_14), .out_15(c8_1_out_15),
    .out_16(c8_1_out_16), .out_17(c8_1_out_17), .in_1(rom_2_data[6]));
  C8 c8_2 (
    .in_2(\n8加法_1_out_25 ), .in_3(\n8加法_1_out_24 ), .in_4(\n8加法_1_out_23 ), .in_5(\n8加法_1_out_22 ),
    .in_6(\n8加法_1_out_21 ), .in_7(\n8加法_1_out_20 ), .in_8(\n8加法_1_out_19 ), .in_9(\n8加法_1_out_18 ),
    .out_10(c8_1_out_17), .out_11(c8_1_out_16), .out_12(c8_1_out_15), .out_13(c8_1_out_14),
    .out_14(c8_1_out_13), .out_15(c8_1_out_12), .out_16(c8_1_out_11), .out_17(c8_1_out_10),
    .in_1(rom_2_data[4]));
  C8 c8_3 (
    .in_2(reg8_2_out_17), .in_3(reg8_2_out_16), .in_4(reg8_2_out_15), .in_5(reg8_2_out_14),
    .in_6(reg8_2_out_13), .in_7(reg8_2_out_12), .in_8(reg8_2_out_11), .in_9(reg8_2_out_10),
    .out_10(double_16key_1_out_37), .out_11(double_16key_1_out_38), .out_12(double_16key_1_out_39),
    .out_13(double_16key_1_out_40), .out_14(double_16key_1_out_41), .out_15(double_16key_1_out_42),
    .out_16(double_16key_1_out_43), .out_17(double_16key_1_out_44), .in_1(rom_2_data[5]));
  _2seg u_2seg_1 (
    .in_2(double_16key_1_out_37), .in_3(double_16key_1_out_38), .in_4(double_16key_1_out_39),
    .in_5(double_16key_1_out_40), .in_6(double_16key_1_out_41), .in_7(double_16key_1_out_42),
    .in_8(double_16key_1_out_43), .in_9(double_16key_1_out_44), .out_10(n2seg_1_out_10),
    .out_11(n2seg_1_out_11), .out_12(n2seg_1_out_12), .out_13(n2seg_1_out_13), .out_14(n2seg_1_out_14),
    .out_15(n2seg_1_out_15), .out_16(n2seg_1_out_16), .out_17(n2seg_1_out_17), .out_18(n2seg_1_out_18),
    .out_19(n2seg_1_out_19), .out_20(n2seg_1_out_20), .out_21(n2seg_1_out_21), .out_22(n2seg_1_out_22),
    .out_23(n2seg_1_out_23), .in_1(rom_2_data[0]));
  \_8加法  \u_8加法_1  (
    .in_1(reg8_1_out_10), .in_2(reg8_1_out_11), .in_3(reg8_1_out_12), .in_4(reg8_1_out_13),
    .in_5(reg8_1_out_14), .in_6(reg8_1_out_15), .in_7(reg8_1_out_16), .in_8(reg8_1_out_17),
    .in_9(reg8_3_out_10), .in_10(reg8_3_out_11), .in_11(reg8_3_out_12), .in_12(reg8_3_out_13),
    .in_13(reg8_3_out_14), .in_14(reg8_3_out_15), .in_15(reg8_3_out_16), .in_16(reg8_3_out_17),
    .out_17(out_35), .out_18(\n8加法_1_out_18 ), .out_19(\n8加法_1_out_19 ), .out_20(\n8加法_1_out_20 ),
    .out_21(\n8加法_1_out_21 ), .out_22(\n8加法_1_out_22 ), .out_23(\n8加法_1_out_23 ), .out_24(\n8加法_1_out_24 ),
    .out_25(\n8加法_1_out_25 ));
  reg8 reg8_1 (
    .in_1(reg8_2_out_10), .in_2(reg8_2_out_11), .in_3(reg8_2_out_12), .in_4(reg8_2_out_13),
    .in_5(reg8_2_out_14), .in_6(reg8_2_out_15), .in_7(reg8_2_out_16), .in_9(reg8_2_out_17),
    .in_8(rom_2_data[2]), .out_10(reg8_1_out_10), .out_11(reg8_1_out_11), .out_12(reg8_1_out_12),
    .out_13(reg8_1_out_13), .out_14(reg8_1_out_14), .out_15(reg8_1_out_15), .out_16(reg8_1_out_16),
    .out_17(reg8_1_out_17));
  reg8 reg8_2 (
    .in_1(c8_1_out_17), .in_2(c8_1_out_16), .in_3(c8_1_out_15), .in_4(c8_1_out_14), .in_5(c8_1_out_13),
    .in_6(c8_1_out_12), .in_7(c8_1_out_11), .in_9(c8_1_out_10), .in_8(rom_2_data[3]), .out_10(reg8_2_out_10),
    .out_11(reg8_2_out_11), .out_12(reg8_2_out_12), .out_13(reg8_2_out_13), .out_14(reg8_2_out_14),
    .out_15(reg8_2_out_15), .out_16(reg8_2_out_16), .out_17(reg8_2_out_17));
  reg8 reg8_3 (
    .in_1(reg8_2_out_10), .in_2(reg8_2_out_11), .in_3(reg8_2_out_12), .in_4(reg8_2_out_13),
    .in_5(reg8_2_out_14), .in_6(reg8_2_out_15), .in_7(reg8_2_out_16), .in_9(reg8_2_out_17),
    .in_8(rom_2_data[1]), .out_10(reg8_3_out_10), .out_11(reg8_3_out_11), .out_12(reg8_3_out_12),
    .out_13(reg8_3_out_13), .out_14(reg8_3_out_14), .out_15(reg8_3_out_15), .out_16(reg8_3_out_16),
    .out_17(reg8_3_out_17));
  _7_Segment_Display #(.active("false")) u_7_segment_display_1 (
    .g(n2seg_1_out_16), .f(n2seg_1_out_15), .a(n2seg_1_out_10), .b(n2seg_1_out_11), .e(n2seg_1_out_14),
    .d(n2seg_1_out_13), .c(n2seg_1_out_12), .dp(1'b1));
  _7_Segment_Display #(.active("false")) u_7_segment_display_2 (
    .g(n2seg_1_out_23), .f(n2seg_1_out_22), .a(n2seg_1_out_17), .b(n2seg_1_out_18), .e(n2seg_1_out_21),
    .d(n2seg_1_out_20), .c(n2seg_1_out_19), .dp(1'b1));
  Clock clock_1 (.out(clock_1_out));
  // Probe on counter_1_q
  Counter #(.width(6), .max('h3f)) counter_1 (
    .Q(counter_1_q), .clk(clock_1_out), .clr(rom_2_data[9]));  // open: load, D, count, carry
  // Probe on {rom_1_data, counter_1_q[1:0]}
  // Probe on {rom_1_data, counter_1_q[1:0]}
  // Probe on rom_1_data
  ROM #(.addrWidth(4), .dataWidth(7)) rom_1 (.addr(counter_1_q[5:2]), .data({rom_1_data_2, rom_1_data}));  // open: sel
  // Probe on {rom_1_data_2, rom_1_data}
  ROM #(.addrWidth(5), .dataWidth(11)) rom_2 (.addr({rom_1_data, counter_1_q[1:0]}), .data(rom_2_data));  // open: sel
  // Probe on rom_2_data

  // Notes on the sheet:
  //   contents of rom_1 (hex, n*v repeats v):
  //   14 7 15 2 16 0 0 0 1
  //   contents of rom_2 (hex, n*v repeats v):
  //   4*0 c9 13 19 8*21 0 0 141 149 45 4*21 4*0 c1 c9 13 19
endmodule
